# Fritzing sketch robot-electronics (saved by Fritzing 1.0.3b)
circuit board: 8.46667cm x 5.64444cm

parts:
  Part3 = 16-Channel 12-bit PWM Servo Shield - I2C [part_number=1411]
  JACK1 = 2.1mm Barrel Jack with Terminal Block
  Part4 = Arduino Uno (Rev3) - ICSP  # not connected
  SERVO1 = Tower Pro MG90S servo [part_number=101246]
  C1 = Capacitor Polarized [package=cpol-radial-1000uf-25v]
  SERVO2 = Tower Pro MG90S servo [part_number=101246]
  SERVO3 = Tower Pro MG90S servo [part_number=101246]
  SERVO4 = Tower Pro MG90S servo [part_number=101246]

nets:
  +5V: Part3.5.0V, SERVO1.+5V, C1.+, SERVO2.+5V, SERVO3.+5V, SERVO4.+5V
  GND: Part3.GND, JACK1.NEG, SERVO1.GND, C1.-, SERVO2.GND, SERVO3.GND, SERVO4.GND
  N1: Part3.PWRIN, JACK1.POS
  N2: Part3.PWM7, SERVO3.Signal
  N3: Part3.PWM3, SERVO4.Signal
  N4: Part3.PWM15, SERVO1.Signal
  N5: Part3.PWM11, SERVO2.Signal

notes:
  1000µF 25V
  5V 2A
  J1
  J2
  J4
  J3

custom parts:
  16-Channel 12-bit PWM Servo Shield - I2C: You want to make a cool Arduino robot, maybe a hexapod walker, or maybe just a piece of art with a lot of moving parts. Or maybe you want to drive a lot of LEDs with precise PWM output. This shield is just like our popular PWM/Servo Breakout but now Arduino-ready and works with any Arduino that uses shields: Uno, Leo, Mega, ADK, its all good. Using only two I2C pins, control 16 free-running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
  Tower Pro MG90S servo: Original file by John De Cristofaro http://www.adafruit.com/products/1449 Adafruit Feedback Servo (Small) Edited by: e-radionica.com 28/9/2015
